// Digital circuit CPU.dig as structural Verilog
module CPU (
  input  CLK_RAW,
  input  [31:0] Breakpoint,
  output [31:0] x8_s0,
  output [31:0] x9_s1,
  output [31:0] x10_a0,
  output [31:0] PC,
  output [31:0] Address,
  output [31:0] Instr,
  output [7:0] Data_Read,
  output [5:0] Step,
  output [7:0] Substep,
  output [16:0] out_10,
  output [15:0] out_11,
  output [31:0] A,
  output [31:0] B,
  output [31:0] Result,
  output [11:0] CSR_Address,
  output [31:0] x11_a1,
  output [31:0] x4_tp,
  output [31:0] x5_t0,
  output [31:0] x6_t1,
  output [31:0] x7_t2,
  output [31:0] x1_ra,
  output [31:0] x2_sp,
  output [31:0] x3_gp,
  output [31:0] x12_a2,
  output [31:0] x13_a3,
  output [31:0] x14_a4,
  output [31:0] x15_a5,
  output [31:0] mepc,
  output [31:0] mscratch,
  output [31:0] mstatus,
  output [31:0] mie,
  output [31:0] mip,
  output [31:0] mcause,
  output [10:0] out_35,
  output [31:0] mtvec,
  output [7:0] Data_Write,
  output [31:0] Instr_2,
  output [31:0] Cycles,
  output [15:0] Instr16
);

  wire ADDR_CLK, ADDR_IN, ADDR_LATCH, ALU_A, ALU_AUX, ALU_B, ALU_N, and_1_out, and_2_out, and_5_out, B_INSTR,
       B_RUN, B_STEP, B_STOP, B_SUBSTEP, BUS_CLK, BUS_EN, BUT_INSTR, BUT_STOP, button_1_out, button_2_out,
       CLK, clock_1_lastsubstep, CNT_2, comparator_1_eq, comparator_1_gt, comparator_1_lt, comparator_2_eq,
       CS_IO, CS_RAM, CS_ROM, CSR_ADDR_LATCH, CSR_IN, CSR_IN_LATCH, CSR_OUT, CSR_OUT_LATCH, CSR_PC_OUT,
       d_ff_2_q, d_ff_3_q, d_ff_as_1_q, d_ff_as_3_q, d_ff_as_4_q, diodeforward_1_out, Imm, ImmB, ImmCSR,
       ImmI, ImmJ, ImmS, ImmU, INT1P, INT2P, INT3P, LASTSTEP, LEN4, Mem_Dval, MEM_IN, MEM_OUT, MEPC_OUT,
       mie_1_mei1e, mie_1_mei2e, mie_1_mei3e, MIE_t, mip_1_mei1p, mip_1_mei2p, mip_1_mei3p, MRET, MTVEC_OUT,
       multiplexer_1_out, multiplexer_8_out, nALU_RESET, nCLK, nILL_OP, nILL_OP_FF, nIRQ, nKB_INT, nMEM_OE,
       nMEM_WE, nOPDONE, not_2_out, not_3_out, nREG_IN_EN, nRESET, nS_EXT, nSTEPDONE, nWAIT, nWAIT_DONE,
       nWAKEUP, OP_IMM_LATCH, OP_IN, OP_IN_MUX, OP_LATCH, or_1_out, PC_IN, PC_IN_LATCH, PC_IN_MUX, PC_OUT,
       PC_OUT_LATCH, PC_OUT_SnP, REG_IN, RESET, RS1, Running, SLEEP, Stopped, switch_1_a, TRAP_OP,
       TRAP_OP_SnP;
  wire [0:0] LEN;
  wire [1:0] ALU_A_MUX, REG_IN_MUX, TRAP2;
  wire [2:0] ALU_OP, IMM_MUX;
  wire [3:0] RSA, RSB, RSD;
  wire [7:0] DATA;
  wire [15:0] DATA_ADDR;
  wire [20:18] MicroCode_d;

  // RGBLED rgbled_1: pin names not known; wires that end beside it: Stopped, Running, 1'b0
  Comparator #(.Bits(32)) comparator_1 (
    .a(x3_gp), .b(32'h1), .gt(comparator_1_gt), .eq(comparator_1_eq), .lt(comparator_1_lt));
  and and_1 (and_1_out, nIRQ, nILL_OP_FF);
  D_FF #(.Default(1)) d_ff_1 (.D(nILL_OP), .C(CLK), .Q(nILL_OP_FF));  // open: nQ
  // RGBLED rgbled_2: pin names not known; wires that end beside it: comparator_1_gt, comparator_1_eq, comparator_1_lt
  Comparator #(.Bits(32)) comparator_2 (.a(Breakpoint), .b(PC), .eq(comparator_2_eq));  // open: gt, lt
  Button #(.activeLow("true")) Stop (.out(BUT_STOP));
  Button #(.activeLow("true")) Run (.out(B_RUN));
  Interrupt_Controller interrupt_controller_1 (
    .BUS_CLK(BUS_CLK), .IRQ_OP_SnP(TRAP_OP_SnP), .LASTSTEP(LASTSTEP), .nIRQ(and_1_out), .OP_LATCH(OP_LATCH),
    .nRESET(nRESET), .IRQ_OP(TRAP_OP), .IRQ_OP_FETCH(OP_IN_MUX));
  and and_2 (and_2_out, nRESET, nOPDONE);
  Switch switch_1 (.A(switch_1_a), .B(comparator_1_lt));
  D_FF d_ff_2 (.D(comparator_2_eq), .C(nOPDONE), .Q(d_ff_2_q));  // open: nQ
  PullUp pullup_1 (.out(switch_1_a));
  D_FF_AS #(.Default(1)) d_ff_as_1 (.Set(nCLK), .D(1'b0), .C(d_ff_2_q), .Clr(1'b0), .Q(d_ff_as_1_q));  // open: nQ
  D_FF_AS d_ff_as_2 (.Set(~1'b1), .D(1'b1), .C(ADDR_LATCH), .Clr(~and_2_out), .Q(TRAP_OP_SnP));  // open: nQ
  Button #(.activeLow("true")) One_Instruction (.out(BUT_INSTR));
  Button #(.activeLow("true")) One_Step (.out(B_STEP));
  Button #(.activeLow("true")) One_Substep (.out(B_SUBSTEP));
  D_FF #(.Default(1)) d_ff_3 (.D(switch_1_a), .C(~nOPDONE), .Q(d_ff_3_q));  // open: nQ
  DiodeBackward diodebackward_1 (.in(d_ff_3_q), .out(B_STOP));
  DiodeBackward diodebackward_2 (.in(BUT_STOP), .out(B_STOP));
  DiodeBackward diodebackward_3 (.in(d_ff_as_1_q), .out(B_INSTR));
  DiodeBackward diodebackward_4 (.in(BUT_INSTR), .out(B_INSTR));
  PullUp pullup_2 (.out(B_STOP));
  PullUp pullup_3 (.out(B_INSTR));
  Reset reset_1 (.out(nRESET));
  Reset #(.invertOutput("false")) reset_2 (.out(RESET));
  Multiplexer multiplexer_1 (.sel(ALU_A_MUX[0]), .in_0(RS1), .in_1(PC_OUT), .out(multiplexer_1_out));
  DebugShift32 debugshift32_1 (.CLK(BUS_CLK), .D(ALU_A), .nEN(1'b0), .Val(A));
  DebugShift32 debugshift32_2 (.CLK(BUS_CLK), .D(ALU_B), .nEN(1'b0), .Val(B));
  D_FF #(.Bits(8)) d_ff_4 (.D(DATA), .C(nMEM_OE), .Q(Data_Read));  // open: nQ
  D_FF #(.Bits(8)) d_ff_5 (.D(DATA), .C(nMEM_WE), .Q(Data_Write));  // open: nQ
  Multiplexer multiplexer_2 (.sel(ALU_A_MUX[1]), .in_0(multiplexer_1_out), .in_1(ALU_A_MUX[0]), .out(ALU_A));
  // Mem mem_1: pin names not known; wires that end beside it: CLK, nCLK, BUS_CLK, MEM_IN, ADDR_IN, ADDR_LATCH, ADDR_CLK, nMEM_OE, nMEM_WE, nS_EXT, nRESET, MEM_OUT, DATA, DATA_ADDR, CS_ROM, CS_RAM, CS_IO, Address, Mem_Dval
  DiodeBackward diodebackward_5 (.in(nMEM_OE), .out(nWAIT));
  DiodeBackward diodebackward_6 (.in(nMEM_WE), .out(nWAIT));
  // Clock_driver clock_driver_1: pin names not known; wires that end beside it: CLK_RAW, B_STOP, B_RUN, B_INSTR, B_STEP, B_SUBSTEP, nSTEPDONE, OP_LATCH, nRESET, nWAKEUP, SLEEP, nWAIT_DONE, nWAIT, CLK, nCLK, Running
  PullUp pullup_4 (.out(nWAIT));
  nand nand_1 (LEN4, LEN[0], BUS_EN);
  or or_1 (or_1_out, IMM_MUX[0], IMM_MUX[1], IMM_MUX[2]);
  DebugShift32 debugshift32_3 (.CLK(BUS_CLK), .D(ADDR_IN), .nEN(1'b0), .Val(Result));
  Multiplexer multiplexer_3 (.sel(or_1_out), .in_0(MEM_IN), .in_1(Imm), .out(ALU_B));
  not not_1 (Stopped, Running);
  DiodeBackward diodebackward_7 (.in(CS_ROM), .out(nWAIT_DONE));
  DiodeBackward diodebackward_8 (.in(CS_RAM), .out(nWAIT_DONE));
  DiodeBackward diodebackward_9 (.in(CS_IO), .out(nWAIT_DONE));
  nor nor_1 (LASTSTEP, LEN[0], BUS_EN);
  PullUp pullup_5 (.out(nWAIT_DONE));
  Clock clock_1 (
    .CLK(CLK), .nCLK(nCLK), .nLEN4(LEN4), .LASTSTEP(LASTSTEP), .SUBSTEP_EN(1'b1), .nRESET(nRESET),
    .STEP(out_10[5:0]), .LASTSUBSTEP(clock_1_lastsubstep), .nSTEPDONE(nSTEPDONE), .SUBSTEP(Substep),
    .nOPDONE(nOPDONE));
  ALU alu_1 (
    .BUS_CLK(BUS_CLK), .A(ALU_A), .B(ALU_B), .N(ALU_N), .ALU_nRESET(nALU_RESET), .ALU_AUX(ALU_AUX),
    .S(ALU_OP), .FLAG(out_10[16]), .OUT(ADDR_IN));  // open: DLEN, DSUM, C
  Terminal terminal_1 (.A(DATA_ADDR), .nCS(CS_IO), .nWE(nMEM_WE), .nOE(nMEM_OE), .D(DATA), .nINT(nKB_INT));
  EEPROM #(.AddrBits(16), .Bits(8)) Firmware (.A(DATA_ADDR), .CS(~CS_ROM), .WE(~nMEM_WE), .OE(~nMEM_OE), .D(DATA));
  RAMSinglePortSel #(.AddrBits(16), .Bits(8)) RAM (.A(DATA_ADDR), .CS(~CS_RAM), .WE(~nMEM_WE), .OE(~nMEM_OE), .D(DATA));
  and and_3 (BUS_CLK, CLK, BUS_EN);
  Multiplexer multiplexer_4 (.sel(PC_IN_MUX), .in_0(ADDR_IN), .in_1(CSR_PC_OUT), .out(PC_IN));
  Multiplexer multiplexer_5 (.sel(OP_IN_MUX), .in_0(MEM_OUT), .in_1(TRAP_OP), .out(OP_IN));
  D_FF d_ff_6 (.D(OP_LATCH), .C(CLK), .Q(OP_IMM_LATCH));  // open: nQ
  Multiplexer #(.Selector_Bits(3)) multiplexer_6 (
    .sel(IMM_MUX), .in_0(ImmCSR), .in_1(ImmI), .in_2(ImmS), .in_3(ImmB), .in_4(ImmU), .in_5(ImmJ),
    .in_6(1'b0), .in_7(1'b1), .out(Imm));
  ROM #(.AddrBits(17), .isProgramMemory("true"), .Bits(32)) MicroCode (
    .A(out_10), .sel(1'b1),
    .D({REG_IN_MUX, IMM_MUX, ALU_A_MUX, PC_IN_MUX, CSR_IN_LATCH, CSR_OUT_LATCH, CSR_ADDR_LATCH, MicroCode_d, nALU_RESET, ALU_AUX, ALU_OP, ALU_N, nREG_IN_EN, nMEM_WE, nMEM_OE, ADDR_CLK, ADDR_LATCH, nILL_OP, PC_OUT_SnP, PC_IN_LATCH, OP_LATCH, SLEEP, BUS_EN, LEN[0]}));
  PC pc_1 (
    .CLK(CLK), .BUS_CLK(BUS_CLK), .IN(PC_IN), .LATCH_IN(PC_IN_LATCH), .LATCH_OUT(PC_OUT_LATCH),
    .SnP_OUT(PC_OUT_SnP), .nPE_CNT(OP_LATCH), .EN_CNT(CNT_2), .nRESET(nRESET), .OUT(PC_OUT), .PC(PC));
  OpCode opcode_1 (
    .BUS_CLK(BUS_CLK), .IN(OP_IN), .OP_LATCH(OP_LATCH), .IMM_LATCH(OP_IMM_LATCH), .IMM_SnP(BUS_EN),
    .nRESET(nRESET), .ImmI(ImmI), .ImmS(ImmS), .ImmB(ImmB), .ImmU(ImmU), .ImmJ(ImmJ), .ImmCSR(ImmCSR),
    .RSA(RSA), .RSB(RSB), .RD(RSD), .OPCODE(out_10[10:6]), .FUNC3(out_10[13:11]), .ALU_SA(out_10[15]),
    .nS_EXT(nS_EXT), .SYS(out_10[14]), .TRAP2(TRAP2), .CNT_2(CNT_2), .Instr(Instr), .DImmI(out_11),
    .Instr16(Instr16));
  and and_4 (PC_OUT_LATCH, nILL_OP_FF, LASTSTEP);
  // Register_bank register_bank_1: pin names not known; wires that end beside it: BUS_CLK, REG_IN, nREG_IN_EN, RSA, RSB, RSD, RESET, RS1, MEM_IN
  Register_view register_view_1 (
    .BUS_CLK(BUS_CLK), .nREG_IN_EN(nREG_IN_EN), .REG_IN(REG_IN), .RSD(RSD), .x1_ra(x1_ra), .x2_sp(x2_sp),
    .x3_gp(x3_gp), .x4_tp(x4_tp), .x5_t0(x5_t0), .x6_t1(x6_t1), .x7_t2(x7_t2), .x8_s0_fp(x8_s0),
    .x9_s1(x9_s1), .x10_a0(x10_a0), .x11_a1(x11_a1), .x12_a2(x12_a2), .x13_a3(x13_a3), .x14_a4(x14_a4),
    .x15_a5(x15_a5));
  Multiplexer #(.Selector_Bits(2)) multiplexer_7 (
    .sel(REG_IN_MUX), .in_0(ADDR_IN), .in_1(MEM_OUT), .in_2(CSR_IN), .in_3(PC_OUT), .out(REG_IN));
  Button #(.activeLow("true")) button_1 (.out(button_1_out));
  Button #(.activeLow("true")) button_2 (.out(button_2_out));
  not not_2 (not_2_out, MRET);
  Multiplexer multiplexer_8 (.sel(out_10[13]), .in_0(RS1), .in_1(Imm), .out(multiplexer_8_out));
  PullDown pulldown_1 (.out(CSR_IN));
  and and_5 (and_5_out, not_2_out, PC_IN_MUX);
  D_FF_AS #(.Default(1)) d_ff_as_3 (.Set(CLK), .D(1'b0), .C(PC_IN_MUX), .Clr(1'b0), .Q(d_ff_as_3_q));  // open: nQ
  Counter #(.Bits(32)) counter_1 (.en(1'b1), .C(CLK), .clr(1'b0), .out(Cycles));  // open: ovf
  MIE mie_1 (
    .CLK(CLK), .BUS_CLK(BUS_CLK), .CSR_IN(CSR_OUT), .CSR_IN_LATCH(CSR_IN_LATCH),
    .CSR_OUT_LATCH(CSR_OUT_LATCH), .CSR_ADDR(CSR_Address), .nRESET(nRESET), .CSR_OUT(CSR_IN), .mie(mie),
    .MEI1E(mie_1_mei1e), .MEI2E(mie_1_mei2e), .MEI3E(mie_1_mei3e));
  MIP mip_1 (
    .CLK(CLK), .BUS_CLK(BUS_CLK), .CSR_IN(CSR_OUT), .CSR_IN_LATCH(CSR_IN_LATCH),
    .CSR_OUT_LATCH(CSR_OUT_LATCH), .CSR_ADDR(CSR_Address), .nINT1(nKB_INT), .nINT2(button_1_out),
    .nINT3(button_2_out), .nRESET(nRESET), .CSR_OUT(CSR_IN), .mip(mip), .MEI1P(mip_1_mei1p),
    .MEI2P(mip_1_mei2p), .MEI3P(mip_1_mei3p));
  MEPC mepc_1 (
    .BUS_CLK(BUS_CLK), .PC_IN(PC_OUT), .IN_EN(and_5_out), .CSR_IN(CSR_OUT), .CSR_IN_LATCH(CSR_IN_LATCH),
    .CSR_ADDR(CSR_Address), .RESET(RESET), .OUT(MEPC_OUT), .CSR_OUT(CSR_IN), .mepc(mepc));
  MSTATUS mstatus_1 (
    .CLK(CLK), .BUS_CLK(BUS_CLK), .CSR_IN(CSR_OUT), .CSR_IN_LATCH(CSR_IN_LATCH),
    .CSR_OUT_LATCH(CSR_OUT_LATCH), .CSR_ADDR(CSR_Address), .IRQ(PC_IN_MUX), .MRET(MRET),
    .IRQ_LATCH(d_ff_as_3_q), .RESET(RESET), .nRESET(nRESET), .CSR_OUT(CSR_IN), .mstatus(mstatus), .MIE(MIE_t));  // open: MPIE
  CSR csr_1 (
    .CLK(BUS_CLK), .INA(multiplexer_8_out), .INB(CSR_IN), .CSR_FUNC(out_10[12:11]), .ADDR_IN(Imm),
    .ADDR_LATCH(CSR_ADDR_LATCH), .nRESET(nRESET), .NEW_VAL(CSR_OUT), .ADDR(CSR_Address));
  Counter #(.Bits(32)) counter_2 (.en(1'b1), .C(~nOPDONE), .clr(1'b0), .out(Instr_2));  // open: ovf
  D_FF_AS #(.Default(1)) d_ff_as_4 (.Set(CLK), .D(MRET), .C(PC_IN_MUX), .Clr(1'b0), .Q(d_ff_as_4_q));  // open: nQ
  and and_6 (INT1P, mie_1_mei1e, mip_1_mei1p);
  and and_7 (INT2P, mie_1_mei2e, mip_1_mei2p);
  and and_8 (INT3P, mie_1_mei3e, mip_1_mei3p);
  not not_3 (not_3_out, TRAP2[0]);
  and and_9 (MRET, not_3_out, TRAP2[1]);
  MTVEC mtvec_1 (
    .BUS_CLK(BUS_CLK), .MTVEC_SnP(PC_IN_MUX), .CSR_IN(CSR_OUT), .CSR_IN_LATCH(CSR_IN_LATCH),
    .CSR_ADDR(CSR_Address), .RESET(RESET), .MTVEC_OUT(MTVEC_OUT), .CSR_OUT(CSR_IN), .mtvec(mtvec));
  MSCRATCH mscratch_1 (
    .BUS_CLK(BUS_CLK), .CSR_IN(CSR_OUT), .CSR_IN_LATCH(CSR_IN_LATCH), .CSR_ADDR(CSR_Address), .RESET(RESET),
    .CSR_OUT(CSR_IN), .mscratch(mscratch));
  MCAUSE mcause_1 (
    .BUS_CLK(BUS_CLK), .CSR_IN_LATCH(CSR_IN_LATCH), .CSR_OUT_LATCH(CSR_OUT_LATCH), .CSR_ADDR(CSR_Address),
    .TRAP2(TRAP2), .nIRQ(nIRQ), .INT1P(INT1P), .INT2P(INT2P), .INT3P(INT3P), .IRQ_LATCH(d_ff_as_4_q),
    .nRESET(nRESET), .CSR_OUT(CSR_IN), .mcause(mcause));
  DiodeForward diodeforward_1 (.in(INT1P), .out(diodeforward_1_out));
  DiodeForward diodeforward_2 (.in(INT2P), .out(diodeforward_1_out));
  DiodeForward diodeforward_3 (.in(INT3P), .out(diodeforward_1_out));
  Multiplexer multiplexer_9 (.sel(MRET), .in_0(MTVEC_OUT), .in_1(MEPC_OUT), .out(CSR_PC_OUT));
  PullDown pulldown_2 (.out(diodeforward_1_out));
  not not_4 (nWAKEUP, diodeforward_1_out);
  nand nand_2 (nIRQ, MIE_t, diodeforward_1_out);

  assign out_35 = out_10[16:6];
  assign Step = out_10[5:0];

  // Other names for the same wires on the sheet: IMM_SnP = BUS_EN; LEN[1] = BUS_EN; PC_CNT_EN = OP_LATCH;
  //   ALU_OUT = ADDR_IN; CntCycles[31:0] = Cycles; CntInstr[31:0] = Instr_2; CSR_ADDR[11:0] = CSR_Address;
  //   Da[31:0] = A; Db[31:0] = B; Dres[31:0] = Result; FLAG = out_10[16]; FUNC3[2:0] = out_10[13:11];
  //   Mem_Addr[31:0] = Address; Mem_Data_R[7:0] = Data_Read; Mem_Data_W[7:0] = Data_Write; OPCODE[4:0] = out_10[10:6];
  //   RS2 = MEM_IN; SA = out_10[15]; SYS = out_10[14]; x1[31:0] = x1_ra; x2[31:0] = x2_sp; x3[31:0] = x3_gp;
  //   x4[31:0] = x4_tp; x5[31:0] = x5_t0; x6[31:0] = x6_t1; x7[31:0] = x7_t2; x8[31:0] = x8_s0; x9[31:0] = x9_s1;
  //   x10[31:0] = x10_a0; x11[31:0] = x11_a1; x12[31:0] = x12_a2; x13[31:0] = x13_a3; x14[31:0] = x14_a4;
  //   x15[31:0] = x15_a5

  // Notes on the sheet:
  //   CLK_RAW: Hz: 10000
  //   Debug
  //   Interrupts
  //   Clock
  //   ALU
  //   Memory
  //   contents of Firmware (hex, n*v repeats v):
  //   9,44,81,40,1,41,33,87,20,0,81,43,89,44,63,10,77,36,85,40,5,41,33,87,20,0,89,43,8d,
  //   44,63,18,77,34,8d,40,1d,41,33,87,20,0,a9,43,91,44,63,10,77,34,81,40,37,81,ff,ff,33,
  //   87,20,0,e1,73,95,44,63,17,77,32,b7,0,0,80,1,41,33,87,20,0,b7,3,0,80,99,44,63,1d,77,
  //   30,b7,0,0,80,37,81,ff,ff,33,87,20,0,b7,83,ff,7f,9d,44,63,12,77,30,81,40,37,81,0,0,
  //   7d,11,33,87,20,0,a1,63,fd,13,a1,44,63,17,77,2e,b7,0,0,80,fd,10,1,41,33,87,20,0,b7,
  //   3,0,80,fd,13,a5,44,63,1b,77,2c,b7,0,0,80,fd,10,37,81,0,0,7d,11,33,87,20,0,b7,83,0,
  //   80,f9,13,a9,44,63,1d,77,2a,b7,0,0,80,37,81,0,0,7d,11,33,87,20,0,b7,83,0,80,fd,13,
  //   ad,44,63,10,77,2a,b7,0,0,80,fd,10,37,81,ff,ff,33,87,20,0,b7,83,ff,7f,fd,13,b1,44,
  //   63,13,77,28,81,40,13,1,f0,ff,33,87,20,0,93,3,f0,ff,b5,44,63,19,77,26,93,0,f0,ff,5,
  //   41,33,87,20,0,81,43,b9,44,63,10,77,26,93,0,f0,ff,13,1,f0,ff,33,87,20,0,93,3,e0,ff,
  //   bd,44,63,15,77,24,85,40,37,1,0,80,7d,11,33,87,20,0,b7,3,0,80,c1,44,63,1a,77,22,b5,
  //   40,2d,41,8a,90,e1,43,c5,44,63,93,70,22,b9,40,2d,41,6,91,e5,43,c9,44,63,1c,71,20,b5,
  //   40,86,90,e9,43,cd,44,63,96,70,20,1,42,b5,40,2d,41,33,87,20,0,13,3,7,0,5,2,89,42,e3,
  //   18,52,fe,e1,43,d1,44,63,17,73,1e,1,42,b9,40,2d,41,33,87,20,0,1,0,13,3,7,0,5,2,89,
  //   42,e3,17,52,fe,e5,43,d5,44,63,17,73,1c,1,42,bd,40,2d,41,33,87,20,0,1,0,1,0,13,3,7,
  //   0,5,2,89,42,e3,16,52,fe,e9,43,d9,44,63,16,73,1a,1,42,b5,40,2d,41,33,87,20,0,5,2,89,
  //   42,e3,1a,52,fe,e1,43,dd,44,63,19,77,18,1,42,b9,40,2d,41,1,0,33,87,20,0,5,2,89,42,
  //   e3,19,52,fe,e5,43,e1,44,63,1b,77,16,1,42,bd,40,2d,41,1,0,1,0,33,87,20,0,5,2,89,42,
  //   e3,18,52,fe,e9,43,e5,44,63,1c,77,14,1,42,b5,40,1,0,2d,41,33,87,20,0,5,2,89,42,e3,
  //   19,52,fe,e1,43,e9,44,63,1e,77,12,1,42,b9,40,1,0,2d,41,1,0,33,87,20,0,5,2,89,42,e3,
  //   18,52,fe,e5,43,ed,44,63,1f,77,10,1,42,bd,40,1,0,1,0,2d,41,33,87,20,0,5,2,89,42,e3,
  //   18,52,fe,e9,43,f1,44,63,10,77,10,1,42,2d,41,b5,40,33,87,20,0,5,2,89,42,e3,1a,52,fe,
  //   e1,43,f5,44,63,13,77,e,1,42,2d,41,b9,40,1,0,33,87,20,0,5,2,89,42,e3,19,52,fe,e5,43,
  //   f9,44,63,15,77,c,1,42,2d,41,bd,40,1,0,1,0,33,87,20,0,5,2,89,42,e3,18,52,fe,e9,43,
  //   fd,44,63,16,77,a,1,42,2d,41,1,0,b5,40,33,87,20,0,5,2,89,42,e3,19,52,fe,e1,43,93,4,
  //   0,2,63,17,77,8,1,42,2d,41,1,0,b9,40,1,0,33,87,20,0,5,2,89,42,e3,18,52,fe,e5,43,93,
  //   4,10,2,63,17,77,6,1,42,2d,41,1,0,1,0,bd,40,33,87,20,0,5,2,89,42,e3,18,52,fe,e9,43,
  //   93,4,20,2,63,17,77,4,bd,40,33,1,10,0,bd,43,93,4,30,2,63,1f,71,2,93,0,0,2,33,81,0,
  //   0,93,3,0,2,93,4,40,2,63,15,71,2,b3,0,0,0,81,43,93,4,50,2,63,9e,70,0,c1,40,79,41,33,
  //   80,20,0,81,43,93,4,60,2,63,15,70,0,63,3,90,0,39,a0,81,c0,93,10,4,1,b3,81,90,0,1,a0,
  //   d,44,81,40,1,41,33,87,20,40,81,43,89,44,63,17,77,34,85,40,5,41,33,87,20,40,81,43,
  //   8d,44,63,1f,77,32,8d,40,1d,41,33,87,20,40,93,3,c0,ff,91,44,63,16,77,32,81,40,37,81,
  //   ff,ff,33,87,20,40,a1,63,95,44,63,1d,77,30,b7,0,0,80,1,41,33,87,20,40,b7,3,0,80,99,
  //   44,63,13,77,30,b7,0,0,80,37,81,ff,ff,33,87,20,40,b7,83,0,80,9d,44,63,18,77,2e,81,
  //   40,37,81,0,0,7d,11,33,87,20,40,e1,73,85,3,a1,44,63,1d,77,2c,b7,0,0,80,fd,10,1,41,
  //   33,87,20,40,b7,3,0,80,fd,13,a5,44,63,11,77,2c,b7,0,0,80,fd,10,37,81,0,0,7d,11,33,
  //   87,20,40,b7,83,ff,7f,a9,44,63,14,77,2a,b7,0,0,80,37,81,0,0,7d,11,33,87,20,40,b7,83,
  //   ff,7f,85,3,ad,44,63,17,77,28,b7,0,0,80,fd,10,37,81,ff,ff,33,87,20,40,b7,83,0,80,fd,
  //   13,b1,44,63,1a,77,26,81,40,13,1,f0,ff,33,87,20,40,85,43,b5,44,63,11,77,26,93,0,f0,
  //   ff,5,41,33,87,20,40,93,3,e0,ff,b9,44,63,17,77,24,93,0,f0,ff,13,1,f0,ff,33,87,20,40,
  //   81,43,bd,44,63,1d,77,22,b5,40,2d,41,b3,80,20,40,89,43,c1,44,63,95,70,22,b9,40,2d,
  //   41,33,81,20,40,8d,43,c5,44,63,1d,71,20,b5,40,b3,80,10,40,81,43,c9,44,63,96,70,20,
  //   1,42,b5,40,2d,41,33,87,20,40,13,3,7,0,5,2,89,42,e3,18,52,fe,89,43,cd,44,63,17,73,
  //   1e,1,42,b9,40,2d,41,33,87,20,40,1,0,13,3,7,0,5,2,89,42,e3,17,52,fe,8d,43,d1,44,63,
  //   17,73,1c,1,42,bd,40,2d,41,33,87,20,40,1,0,1,0,13,3,7,0,5,2,89,42,e3,16,52,fe,91,43,
  //   d5,44,63,16,73,1a,1,42,b5,40,2d,41,33,87,20,40,5,2,89,42,e3,1a,52,fe,89,43,d9,44,
  //   63,19,77,18,1,42,b9,40,2d,41,1,0,33,87,20,40,5,2,89,42,e3,19,52,fe,8d,43,dd,44,63,
  //   1b,77,16,1,42,bd,40,2d,41,1,0,1,0,33,87,20,40,5,2,89,42,e3,18,52,fe,91,43,e1,44,63,
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  //   PC
  //   Opcode
  //   Microcode
  //   contents of MicroCode (hex, n*v repeats v):
  //   32832e63,32832e63,32832e63,32832e63,32832e63,32832e63,32832e63,32832e63,830ec1,830f41,
  //   830c41,830e43,830f43,830c41,830e43,830f43,830c41,830e43,830f43,830c41,830e43,830e43,
  //   830e49,810e41,8830e43,8830e43,8830e43,8830e43,8830e43,8830e43,8830e43,8830e43,830ec1,
  //   830f41,830c41,40830643,40830743,40830643,40830643,40830643,40830643,40830643,40830643,
  //   40830640,0,0,0,0,0,0,0,0,0,0,0,0,0,0,0,0,0,0,0,0,32832e63,32832e63,32832e63,32832e63,
  //   32832e63,32832e63,32832e63,32832e63,830ec1,830f41,830c41,830e43,830f43,830c41,830e43,
  //   830f43,830c41,830e43,830f43,830c41,830e43,830e43,830e49,830e41,830e01,830e00,0,0,
  //   0,0,0,0,0,0,0,0,0,0,0,0,0,0,0,0,0,0,0,0,0,0,0,0,0,0,0,0,0,0,0,0,0,0,0,0,32832e63,
  //   32832e63,32832e63,32832e63,32832e63,32832e63,32832e63,32832e63,830ec1,830f41,830c41,
  //   830e43,830f43,830c41,830e43,830f43,830c41,830e43,830f43,830c41,830e43,830e43,830e49,
  //   830e41,830e01,830e00,0,0,0,0,0,0,0,0,0,0,0,0,0,0,0,0,0,0,0,0,0,0,0,0,0,0,0,0,0,0,
  //   0,0,0,0,0,0,0,0,32832e63,32832e63,32832e63,32832e63,32832e63,32832e63,32832e63,32832e63,
  //   830ec1,830f41,830c41,830e43,830f43,830c41,830e43,830f43,830c41,830e43,830f43,830c41,
  //   830e43,830e43,830e49,830e48,0,0,0,0,0,0,0,0,0,0,0,0,0,0,0,0,0,0,0,0,0,0,0,0,0,0,0,
  //   0,0,0,0,0,0,0,0,0,0,0,0,0,32832e63,32832e63,32832e63,32832e63,32832e63,32832e63,32832e63,
  //   32832e63,830ec1,830f41,830c41,830e43,830f43,830c41,830e43,830f43,830c41,830e43,830f43,
  //   830c41,830e43,830e43,830e49,810e41,8830643,8830643,8830643,8830643,8830643,8830643,
  //   8830643,8830643,830e40,0,0,0,0,0,0,0,0,0,0,0,0,0,0,0,0,0,0,0,0,0,0,0,0,0,0,0,0,0,
  //   0,0,32832e63,32832e63,32832e63,32832e63,32832e63,32832e63,32832e63,32832e63,830ec1,
  //   830f41,830c41,830e43,830f43,830c41,830e43,830f43,830c41,830e43,830f43,830c41,830e43,
  //   830e43,830e49,810e41,22830663,22830663,22830663,22830663,22830663,22830663,22830663,
  //   22830663,830e40,0,0,0,0,0,0,0,0,0,0,0,0,0,0,0,0,0,0,0,0,0,0,0,0,0,0,0,0,0,0,0,32832e63,
  //   32832e63,32832e63,32832e63,32832e63,32832e63,32832e63,32832e63,830ec1,830f41,830c41,
  //   830e43,830f43,830c41,830e43,830f43,830c41,830e43,830f43,830c41,830e43,830e43,830e49,
  //   830e41,830e01,830e00,0,0,0,0,0,0,0,0,0,0,0,0,0,0,0,0,0,0,0,0,0,0,0,0,0,0,0,0,0,0,
  //   0,0,0,0,0,0,0,0,32832e63,32832e63,32832e63,32832e63,32832e63,32832e63,32832e63,32832e63,
  //   830ec1,830f41,830c41,830e43,830f43,830c41,830e43,830f43,830c41,830e43,830f43,830c41,
  //   830e43,830e43,830e49,830e41,830e01,830e00,0,0,0,0,0,0,0,0,0,0,0,0,0,0,0,0,0,0,0,0,
  //   0,0,0,0,0,0,0,0,0,0,0,0,0,0,0,0,0,0,32832e63,32832e63,32832e63,32832e63,32832e63,
  //   32832e63,32832e63,32832e63,830ec1,830f41,830c41,830e43,830f43,830c41,830e43,830f43,
  //   830c41,830e43,830f43,830c41,830e43,830e43,830e49,810e41,10830e43,10830e43,10830e43,
  //   10830e43,10830e43,10830e43,10830e43,10830e43,830ec3,830f43,830a41,830a43,830a43,830a43,
  //   830a43,830a43,830a43,830e40,0,0,0,0,0,0,0,0,0,0,0,0,0,0,0,0,0,0,0,0,0,0,32832e63,
  //   32832e63,32832e63,32832e63,32832e63,32832e63,32832e63,32832e63,830ec1,830f41,830c41,
  //   830e43,830f43,830c41,830e43,830f43,830c41,830e43,830f43,830c41,830e43,830e43,830e49,
  //   830e41,830e01,830e00,0,0,0,0,0,0,0,0,0,0,0,0,0,0,0,0,0,0,0,0,0,0,0,0,0,0,0,0,0,0,
  //   0,0,0,0,0,0,0,0,32832e63,32832e63,32832e63,32832e63,32832e63,32832e63,32832e63,32832e63,
  //   830ec1,830f41,830c41,830e43,830f43,830c41,830e43,830f43,830c41,830e43,830f43,830c41,
  //   830e43,830e43,830e49,830e41,830e01,830e00,0,0,0,0,0,0,0,0,0,0,0,0,0,0,0,0,0,0,0,0,
  //   0,0,0,0,0,0,0,0,0,0,0,0,0,0,0,0,0,0,32832e63,32832e63,32832e63,32832e63,32832e63,
  //   32832e63,32832e63,32832e63,830ec1,830f41,830c41,830e43,830f43,830c41,830e43,830f43,
  //   830c41,830e43,830f43,830c41,830e43,830e43,830e49,830e41,830e01,830e00,0,0,0,0,0,0,
  //   0,0,0,0,0,0,0,0,0,0,0,0,0,0,0,0,0,0,0,0,0,0,0,0,0,0,0,0,0,0,0,0,32832e63,32832e63,
  //   32832e63,32832e63,32832e63,32832e63,32832e63,32832e63,830ec1,830f41,830c41,830e43,
  //   830f43,830c41,830e43,830f43,830c41,830e43,830f43,830c41,830e43,830e43,830e49,810e41,
  //   830643,830643,830643,830643,830643,830643,830643,830643,830e40,0,0,0,0,0,0,0,0,0,
  //   0,0,0,0,0,0,0,0,0,0,0,0,0,0,0,0,0,0,0,0,0,0,32832e63,32832e63,32832e63,32832e63,32832e63,
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  //   Registers
  //   CSR
endmodule
